# Fritzing sketch circuits (saved by Fritzing 0.9.4)

parts:
  MH-ET_Live_Minikit_for_ESP1 = MH-ET Live Minikit for ESP32
  SERVO1 = Tower Pro SG90 servo [part_number=101246]

nets:
  GND: MH-ET_Live_Minikit_for_ESP1.GND, SERVO1.GND
  VCC: MH-ET_Live_Minikit_for_ESP1.VCC, SERVO1.+5V
  N1: MH-ET_Live_Minikit_for_ESP1.TDO, SERVO1.Signal

custom parts:
  MH-ET Live Minikit for ESP32: MH-ET Live Minikit for ESP32 ( http://mh.nodebb.com/topic/8/mh-et-live-minikit-for-esp32/2/) PCB footprint is invalid.
  Tower Pro SG90 servo: Original file by John De Cristofaro http://www.adafruit.com/products/1449 Adafruit Feedback Servo (Small) Edited by: e-radionica.com 28/9/2015
